// Logisim project Project 1 Multi version.circ as structural Verilog: 5 circuits, main circuit main
module main (
);

  wire clock10_1__0, clock10_1__1, clock10_1__2, clock10_1__3, clock16_1_w, clock16_1_x, clock16_1_y,
       clock16_1_z, hexadecimal_1_a, hexadecimal_1_b, hexadecimal_1_c, hexadecimal_1_d, hexadecimal_1_e,
       hexadecimal_1_f, hexadecimal_1_g, n7_segment_controller_1_1_a, n7_segment_controller_1_1_b,
       n7_segment_controller_1_1_c, n7_segment_controller_1_1_d, n7_segment_controller_1_1_e,
       n7_segment_controller_1_1_f, n7_segment_controller_1_1_g;

  Clock10 clock10_1 (._0(clock10_1__0), ._1(clock10_1__1), ._2(clock10_1__2), ._3(clock10_1__3));
  Clock16 clock16_1 (.Z(clock16_1_z), .Y(clock16_1_y), .X(clock16_1_x), .W(clock16_1_w));
  _7_Segment_Controller_1 u_7_segment_controller_1_1 (
    .W(clock10_1__3), .X(clock10_1__2), .Y(clock10_1__1), .Z(clock10_1__0), .A(n7_segment_controller_1_1_a),
    .B(n7_segment_controller_1_1_b), .C(n7_segment_controller_1_1_c), .D(n7_segment_controller_1_1_d),
    .E(n7_segment_controller_1_1_e), .F(n7_segment_controller_1_1_f), .G(n7_segment_controller_1_1_g));
  hexadecimal hexadecimal_1 (
    .w(clock16_1_w), .x(clock16_1_x), .y(clock16_1_y), .z(clock16_1_z), .a(hexadecimal_1_a),
    .b(hexadecimal_1_b), .c(hexadecimal_1_c), .d(hexadecimal_1_d), .e(hexadecimal_1_e), .f(hexadecimal_1_f),
    .g(hexadecimal_1_g));
  _7_Segment_Display u_7_segment_display_1 (
    .g(n7_segment_controller_1_1_g), .f(n7_segment_controller_1_1_f), .a(n7_segment_controller_1_1_a),
    .b(n7_segment_controller_1_1_b), .e(n7_segment_controller_1_1_e), .d(n7_segment_controller_1_1_d),
    .c(n7_segment_controller_1_1_c));  // open: dp
  _7_Segment_Display u_7_segment_display_2 (
    .g(hexadecimal_1_g), .f(hexadecimal_1_f), .a(hexadecimal_1_a), .b(hexadecimal_1_b), .e(hexadecimal_1_e),
    .d(hexadecimal_1_d), .c(hexadecimal_1_c));  // open: dp
endmodule

module Clock10 (
  output _0,
  output _1,
  output _2,
  output _3
);

  wire and_1_out, Clock_out;

  Counter #(.width(4), .max('hf)) counter_1 (
    .Q({_3, _2, _1, _0}), .clk(Clock_out), .clr(and_1_out));  // open: load, D, count, carry
  Clock Clock (.out(Clock_out));
  and and_1 (and_1_out, ~_0, _1, ~_2, _3);  // AND_Gate
endmodule

module _7_Segment_Controller_1 (
  input  W,
  input  X,
  input  Y,
  input  Z,
  output A,
  output B,
  output C,
  output D,
  output E,
  output F,
  output G
);

  wire and_1_out, and_2_out, and_3_out, and_4_out, and_5_out, and_6_out, and_7_out, and_8_out, and_9_out,
       and_10_out, and_11_out, and_12_out, and_13_out, and_14_out, and_15_out, and_16_out, and_17_out,
       and_18_out, not_1_out, not_2_out, not_3_out, not_4_out;

  not not_1 (not_1_out, Z);
  not not_2 (not_2_out, X);
  not not_3 (not_3_out, Y);
  not not_4 (not_4_out, W);
  and and_1 (and_1_out, X, Z);
  and and_2 (and_2_out, not_2_out, not_1_out);
  and and_3 (and_3_out, not_3_out, not_1_out);
  and and_4 (and_4_out, Y, Z);
  and and_5 (and_5_out, not_2_out, not_1_out);
  and and_6 (and_6_out, not_2_out, Y);
  and and_7 (and_7_out, Y, not_1_out);
  and and_8 (and_8_out, X, not_3_out, Z);
  and and_9 (and_9_out, not_2_out, not_1_out);
  and and_10 (and_10_out, Y, not_1_out);
  and and_11 (and_11_out, W, not_1_out);
  and and_12 (and_12_out, X, not_1_out);
  and and_13 (and_13_out, X, not_3_out);
  and and_14 (and_14_out, not_3_out, not_1_out);
  and and_15 (and_15_out, not_2_out, Y);
  and and_16 (and_16_out, X, not_3_out);
  and and_17 (and_17_out, Y, not_1_out);
  and and_18 (and_18_out, X, not_1_out);
  or or_1 (A, W, Y, and_1_out, and_2_out);
  or or_2 (B, W, not_2_out, and_3_out, and_4_out);
  or or_3 (C, not_3_out, Z, X, W);
  or or_4 (D, and_5_out, and_6_out, W, and_7_out, and_8_out);
  or or_5 (E, and_9_out, and_10_out, and_11_out);
  or or_6 (F, W, and_12_out, and_13_out, and_14_out);
  or or_7 (G, and_15_out, and_16_out, W, and_17_out, and_18_out);
endmodule

module Clock16 (
  output Z,
  output Y,
  output X,
  output W
);

  wire Clock_out;

  Counter #(.width(4), .max('hf)) counter_1 (.Q({W, X, Y, Z}), .clk(Clock_out));  // open: load, D, count, carry, clr
  Clock Clock (.out(Clock_out));
endmodule

module hexadecimal (
  input  w,
  input  x,
  input  y,
  input  z,
  output a,
  output b,
  output c,
  output d,
  output e,
  output f,
  output g
);

  wire and_1_out, and_2_out, and_3_out, and_4_out, and_5_out, and_6_out, and_7_out, and_8_out, and_9_out,
       and_10_out, and_11_out, and_12_out, and_13_out, and_14_out, and_15_out, and_16_out, and_17_out,
       and_18_out, and_19_out, and_20_out, and_21_out, and_22_out, and_23_out, and_24_out, and_25_out,
       and_26_out, and_27_out, and_28_out, and_29_out, and_30_out, and_31_out, and_32_out, and_33_out,
       and_34_out, and_35_out, not_1_out, not_2_out, not_3_out, not_4_out, not_5_out, not_6_out, not_7_out,
       not_8_out, not_9_out, not_10_out, not_11_out, not_12_out, not_13_out, not_14_out, not_15_out,
       not_16_out, not_17_out, not_18_out, not_19_out, not_20_out, not_21_out, not_22_out, not_23_out,
       not_24_out, not_25_out, not_26_out, not_27_out, not_28_out, not_29_out, not_30_out, not_31_out,
       not_32_out, not_33_out, not_34_out, not_35_out, not_36_out, not_37_out, not_38_out, not_39_out,
       not_40_out, not_41_out, not_42_out, not_43_out;

  not not_1 (not_1_out, x);
  and and_1 (and_1_out, not_1_out, not_2_out);
  not not_2 (not_2_out, z);
  not not_3 (not_3_out, w);
  and and_2 (and_2_out, not_3_out, y);
  not not_4 (not_4_out, w);
  and and_3 (and_3_out, not_4_out, x, z);
  and and_4 (and_4_out, x, y);
  and and_5 (and_5_out, w, not_5_out, not_6_out);
  not not_5 (not_5_out, x);
  not not_6 (not_6_out, y);
  and and_6 (and_6_out, w, not_7_out);
  not not_7 (not_7_out, z);
  not not_8 (not_8_out, w);
  and and_7 (and_7_out, not_8_out, not_9_out);
  not not_9 (not_9_out, x);
  not not_10 (not_10_out, w);
  and and_8 (and_8_out, not_10_out, not_11_out, not_12_out);
  not not_11 (not_11_out, y);
  not not_12 (not_12_out, z);
  not not_13 (not_13_out, x);
  and and_9 (and_9_out, not_13_out, not_14_out);
  not not_14 (not_14_out, z);
  not not_15 (not_15_out, w);
  and and_10 (and_10_out, not_15_out, y, z);
  not not_16 (not_16_out, y);
  and and_11 (and_11_out, w, not_16_out, z);
  not not_17 (not_17_out, w);
  and and_12 (and_12_out, not_17_out, not_18_out);
  not not_18 (not_18_out, y);
  not not_19 (not_19_out, w);
  and and_13 (and_13_out, not_19_out, z);
  not not_20 (not_20_out, y);
  and and_14 (and_14_out, not_20_out, z);
  not not_21 (not_21_out, w);
  and and_15 (and_15_out, not_21_out, x);
  and and_16 (and_16_out, w, not_22_out);
  not not_22 (not_22_out, x);
  not not_23 (not_23_out, w);
  not not_24 (not_24_out, x);
  and and_17 (and_17_out, not_23_out, not_24_out, not_25_out);
  not not_25 (not_25_out, z);
  not not_26 (not_26_out, x);
  and and_18 (and_18_out, not_26_out, y, z);
  and and_19 (and_19_out, x, not_27_out, z);
  not not_27 (not_27_out, y);
  and and_20 (and_20_out, x, y, not_28_out);
  not not_28 (not_28_out, z);
  and and_21 (and_21_out, w, not_29_out);
  not not_29 (not_29_out, y);
  not not_30 (not_30_out, x);
  and and_22 (and_22_out, not_30_out, not_31_out);
  not not_31 (not_31_out, z);
  and and_23 (and_23_out, y, not_32_out);
  not not_32 (not_32_out, z);
  and and_24 (and_24_out, w, y);
  and and_25 (and_25_out, w, x);
  not not_33 (not_33_out, y);
  and and_26 (and_26_out, not_33_out, not_34_out);
  not not_34 (not_34_out, z);
  not not_35 (not_35_out, w);
  and and_27 (and_27_out, not_35_out, x, not_36_out);
  not not_36 (not_36_out, y);
  and and_28 (and_28_out, x, not_37_out);
  not not_37 (not_37_out, z);
  and and_29 (and_29_out, w, not_38_out);
  not not_38 (not_38_out, x);
  and and_30 (and_30_out, w, y);
  not not_39 (not_39_out, x);
  and and_31 (and_31_out, not_39_out, y);
  and and_32 (and_32_out, y, not_40_out);
  not not_40 (not_40_out, z);
  not not_41 (not_41_out, w);
  and and_33 (and_33_out, not_41_out, x, not_42_out);
  not not_42 (not_42_out, y);
  and and_34 (and_34_out, w, not_43_out);
  not not_43 (not_43_out, x);
  and and_35 (and_35_out, w, z);
  or or_1 (b, and_7_out, and_8_out, and_9_out, and_10_out, and_11_out);
  or or_2 (c, and_12_out, and_13_out, and_14_out, and_15_out, and_16_out);
  or or_3 (d, and_17_out, and_18_out, and_19_out, and_20_out, and_21_out);
  or or_4 (e, and_22_out, and_23_out, and_24_out, and_25_out);
  or or_5 (f, and_26_out, and_27_out, and_28_out, and_29_out, and_30_out);
  or or_6 (g, and_31_out, and_32_out, and_33_out, and_34_out, and_35_out);
  or or_7 (a, and_1_out, and_2_out, and_3_out, and_4_out, and_5_out, and_6_out);
endmodule
