// Logisim project CSCE 211 Project #1 with Bonus.circ as structural Verilog: 3 circuits, main circuit main
module main (
);

  wire clock_1_out, n2_7_segment_display_1_a1, n2_7_segment_display_1_a2, n2_7_segment_display_1_b1,
       n2_7_segment_display_1_b2, n2_7_segment_display_1_c1, n2_7_segment_display_1_c2,
       n2_7_segment_display_1_d1, n2_7_segment_display_1_d2, n2_7_segment_display_1_e1,
       n2_7_segment_display_1_e2, n2_7_segment_display_1_f1, n2_7_segment_display_1_f2,
       n2_7_segment_display_1_g1, n2_7_segment_display_1_g2, n99clock_1__0, n99clock_1__1, n99clock_1__2,
       n99clock_1__3, n99clock_1__4, n99clock_1__5, n99clock_1__6;

  _99Clock u_99clock_1 (
    .Clock_Input(clock_1_out), ._6(n99clock_1__6), ._5(n99clock_1__5), ._4(n99clock_1__4),
    ._3(n99clock_1__3), ._2(n99clock_1__2), ._1(n99clock_1__1), ._0(n99clock_1__0));  // open: Reset
  Clock clock_1 (.out(clock_1_out));
  _2_7_segment_display u_2_7_segment_display_1 (
    .A1(n2_7_segment_display_1_a1), .B1(n2_7_segment_display_1_b1), .C1(n2_7_segment_display_1_c1),
    .D1(n2_7_segment_display_1_d1), .E1(n2_7_segment_display_1_e1), .F1(n2_7_segment_display_1_f1),
    .G1(n2_7_segment_display_1_g1), .A2(n2_7_segment_display_1_a2), .B2(n2_7_segment_display_1_b2),
    .C2(n2_7_segment_display_1_c2), .D2(n2_7_segment_display_1_d2), .E2(n2_7_segment_display_1_e2),
    .F2(n2_7_segment_display_1_f2), .G2(n2_7_segment_display_1_g2), .T(n99clock_1__6), .U(n99clock_1__5),
    .V(n99clock_1__4), .W(n99clock_1__3), .X(n99clock_1__2), .Y(n99clock_1__1), .Z(n99clock_1__0));
  _7_Segment_Display u_7_segment_display_1 (
    .g(n2_7_segment_display_1_g1), .f(n2_7_segment_display_1_f1), .a(n2_7_segment_display_1_a1),
    .b(n2_7_segment_display_1_b1), .e(n2_7_segment_display_1_e1), .d(n2_7_segment_display_1_d1),
    .c(n2_7_segment_display_1_c1));  // open: dp
  _7_Segment_Display u_7_segment_display_2 (
    .g(n2_7_segment_display_1_g2), .f(n2_7_segment_display_1_f2), .a(n2_7_segment_display_1_a2),
    .b(n2_7_segment_display_1_b2), .e(n2_7_segment_display_1_e2), .d(n2_7_segment_display_1_d2),
    .c(n2_7_segment_display_1_c2));  // open: dp
endmodule

module _2_7_segment_display (
  input  T,
  input  U,
  input  V,
  input  W,
  input  X,
  input  Y,
  input  Z,
  output A1,
  output B1,
  output C1,
  output D1,
  output E1,
  output F1,
  output G1,
  output A2,
  output B2,
  output C2,
  output D2,
  output E2,
  output F2,
  output G2
);

  wire and_1_out, and_2_out, and_3_out, and_4_out, and_5_out, and_6_out, and_7_out, and_8_out, and_9_out,
       and_10_out, and_11_out, and_12_out, and_13_out, and_14_out, and_15_out, and_16_out, and_17_out,
       and_18_out, and_19_out, and_20_out, and_21_out, and_22_out, and_23_out, and_24_out, and_25_out,
       and_26_out, and_27_out, and_28_out, and_29_out, and_30_out, and_31_out, and_32_out, and_33_out,
       and_34_out, and_35_out, and_36_out, and_37_out, and_38_out, and_39_out, and_40_out, multiplexer_1_out,
       multiplexer_2_out, multiplexer_3_out, multiplexer_4_out, multiplexer_5_out, multiplexer_6_out,
       multiplexer_7_out, multiplexer_8_out, multiplexer_9_out, multiplexer_10_out, multiplexer_11_out,
       multiplexer_12_out, multiplexer_13_out, multiplexer_14_out, multiplexer_15_out, multiplexer_16_out,
       multiplexer_17_out, multiplexer_18_out, multiplexer_19_out, multiplexer_20_out, multiplexer_21_out,
       multiplexer_22_out, multiplexer_23_out, multiplexer_24_out, multiplexer_25_out, multiplexer_26_out,
       multiplexer_27_out, multiplexer_28_out;

  and and_1 (and_1_out, ~W, ~V);  // AND_Gate
  and and_2 (and_2_out, W, V);
  and and_3 (and_3_out, ~W, X);  // AND_Gate
  and and_4 (and_4_out, U, ~W, Y);  // AND_Gate
  and and_5 (and_5_out, ~U, ~V, ~X, ~Y);  // AND_Gate
  and and_6 (and_6_out, ~T, ~X, ~Y, ~W);  // AND_Gate
  and and_7 (and_7_out, ~U, Y, X);  // AND_Gate
  and and_8 (and_8_out, ~T, ~U);  // AND_Gate
  and and_9 (and_9_out, U, ~V);  // AND_Gate
  and and_10 (and_10_out, ~U, W);  // AND_Gate
  and and_11 (and_11_out, ~U, V);  // AND_Gate
  and and_12 (and_12_out, ~W, ~X);  // AND_Gate
  and and_13 (and_13_out, W, X, Y);
  and and_14 (and_14_out, V, W);
  and and_15 (and_15_out, V, X);
  and and_16 (and_16_out, U, ~W, Y);  // AND_Gate
  and and_17 (and_17_out, T, ~W, ~X);  // AND_Gate
  and and_18 (and_18_out, ~V, ~W, ~Y);  // AND_Gate
  and and_19 (and_19_out, ~T, ~V, ~W);  // AND_Gate
  and and_20 (and_20_out, ~T, ~U, ~V, ~X, ~Y);  // AND_Gate
  and and_21 (and_21_out, ~T, ~U, V, X, ~Y);  // AND_Gate
  and and_22 (and_22_out, ~T, ~U, ~V, ~X, ~Y);  // AND_Gate
  and and_23 (and_23_out, ~T, ~U, V, W, ~X);  // AND_Gate
  and and_24 (and_24_out, ~U, V, W, ~X, ~Y);  // AND_Gate
  and and_25 (and_25_out, U, V, W, X);
  and and_26 (and_26_out, ~U, V, ~W, X);  // AND_Gate
  and and_27 (and_27_out, ~T, ~U, ~V, ~W);  // AND_Gate
  and and_28 (and_28_out, T, ~U, ~W, ~X);  // AND_Gate
  and and_29 (and_29_out, ~U, ~V, ~W, ~Y);  // AND_Gate
  and and_30 (and_30_out, ~T, ~U, ~V, ~X, ~Y);  // AND_Gate
  and and_31 (and_31_out, ~T, ~U, ~V, ~W);  // AND_Gate
  and and_32 (and_32_out, ~U, ~V, ~W, ~Y);  // AND_Gate
  and and_33 (and_33_out, T, ~W, ~X);  // AND_Gate
  and and_34 (and_34_out, U, W);
  and and_35 (and_35_out, U, V);
  and and_36 (and_36_out, T, V);
  and and_37 (and_37_out, T, ~W, ~Y);  // AND_Gate
  and and_38 (and_38_out, T, ~W, ~X);  // AND_Gate
  and and_39 (and_39_out, V, W);
  and and_40 (and_40_out, V, X);
  Multiplexer #(.select(5)) multiplexer_1 (
    .in0(1'b1), .in1(1'b0), .in2(1'b1), .in3(1'b1), .in4(1'b0), .in5(1'b1), .in6(1'b1), .in7(1'b1),
    .in8(1'b1), .in9(1'b1), .in10(1'b1), .in11(1'b0), .in12(1'b1), .in13(1'b1), .in14(1'b0), .in15(1'b1),
    .in16(1'b1), .in17(1'b1), .in18(1'b1), .in19(1'b1), .in20(1'b1), .in21(1'b0), .in22(1'b1), .in23(1'b1),
    .in24(1'b0), .in25(1'b1), .in26(1'b1), .in27(1'b1), .in28(1'b1), .in29(1'b1), .in30(1'b1), .in31(1'b0),
    .out(multiplexer_1_out), .sel({V, W, X, Y, Z}), .en(1'b1));
  Multiplexer #(.select(5)) multiplexer_2 (
    .in0(1'b1), .in1(1'b1), .in2(1'b1), .in3(1'b1), .in4(1'b1), .in5(1'b0), .in6(1'b0), .in7(1'b1),
    .in8(1'b1), .in9(1'b1), .in10(1'b1), .in11(1'b1), .in12(1'b1), .in13(1'b1), .in14(1'b1), .in15(1'b0),
    .in16(1'b0), .in17(1'b1), .in18(1'b1), .in19(1'b1), .in20(1'b1), .in21(1'b1), .in22(1'b1), .in23(1'b1),
    .in24(1'b1), .in25(1'b0), .in26(1'b0), .in27(1'b1), .in28(1'b1), .in29(1'b1), .in30(1'b1), .in31(1'b1),
    .out(multiplexer_2_out), .sel({V, W, X, Y, Z}), .en(1'b1));
  Multiplexer #(.select(5)) multiplexer_3 (
    .in0(1'b1), .in1(1'b1), .in2(1'b0), .in3(1'b1), .in4(1'b1), .in5(1'b1), .in6(1'b1), .in7(1'b1),
    .in8(1'b1), .in9(1'b1), .in10(1'b1), .in11(1'b1), .in12(1'b0), .in13(1'b1), .in14(1'b1), .in15(1'b1),
    .in16(1'b1), .in17(1'b1), .in18(1'b1), .in19(1'b1), .in20(1'b1), .in21(1'b1), .in22(1'b0), .in23(1'b1),
    .in24(1'b1), .in25(1'b1), .in26(1'b1), .in27(1'b1), .in28(1'b1), .in29(1'b1), .in30(1'b1), .in31(1'b1),
    .out(multiplexer_3_out), .sel({V, W, X, Y, Z}), .en(1'b1));
  Multiplexer #(.select(5)) multiplexer_4 (
    .in0(1'b1), .in1(1'b0), .in2(1'b1), .in3(1'b1), .in4(1'b0), .in5(1'b1), .in6(1'b1), .in7(1'b0),
    .in8(1'b1), .in9(1'b1), .in10(1'b1), .in11(1'b0), .in12(1'b1), .in13(1'b1), .in14(1'b0), .in15(1'b1),
    .in16(1'b1), .in17(1'b0), .in18(1'b1), .in19(1'b1), .in20(1'b1), .in21(1'b0), .in22(1'b1), .in23(1'b1),
    .in24(1'b0), .in25(1'b1), .in26(1'b1), .in27(1'b0), .in28(1'b1), .in29(1'b1), .in30(1'b1), .in31(1'b0),
    .out(multiplexer_4_out), .sel({V, W, X, Y, Z}), .en(1'b1));
  Multiplexer #(.select(5)) multiplexer_5 (
    .in0(1'b1), .in1(1'b0), .in2(1'b1), .in3(1'b0), .in4(1'b0), .in5(1'b0), .in6(1'b1), .in7(1'b0),
    .in8(1'b1), .in9(1'b0), .in10(1'b1), .in11(1'b0), .in12(1'b1), .in13(1'b0), .in14(1'b0), .in15(1'b0),
    .in16(1'b1), .in17(1'b0), .in18(1'b1), .in19(1'b0), .in20(1'b1), .in21(1'b0), .in22(1'b1), .in23(1'b0),
    .in24(1'b0), .in25(1'b0), .in26(1'b1), .in27(1'b0), .in28(1'b1), .in29(1'b0), .in30(1'b1), .in31(1'b0),
    .out(multiplexer_5_out), .sel({V, W, X, Y, Z}), .en(1'b1));
  Multiplexer #(.select(5)) multiplexer_6 (
    .in0(1'b1), .in1(1'b0), .in2(1'b0), .in3(1'b0), .in4(1'b1), .in5(1'b1), .in6(1'b1), .in7(1'b0),
    .in8(1'b1), .in9(1'b1), .in10(1'b1), .in11(1'b0), .in12(1'b0), .in13(1'b0), .in14(1'b1), .in15(1'b1),
    .in16(1'b1), .in17(1'b0), .in18(1'b1), .in19(1'b1), .in20(1'b1), .in21(1'b0), .in22(1'b0), .in23(1'b0),
    .in24(1'b1), .in25(1'b1), .in26(1'b1), .in27(1'b0), .in28(1'b1), .in29(1'b1), .in30(1'b1), .in31(1'b0),
    .out(multiplexer_6_out), .sel({V, W, X, Y, Z}), .en(1'b1));
  Multiplexer #(.select(5)) multiplexer_7 (
    .in0(1'b0), .in1(1'b0), .in2(1'b1), .in3(1'b1), .in4(1'b1), .in5(1'b1), .in6(1'b1), .in7(1'b0),
    .in8(1'b1), .in9(1'b1), .in10(1'b0), .in11(1'b0), .in12(1'b1), .in13(1'b1), .in14(1'b1), .in15(1'b1),
    .in16(1'b1), .in17(1'b0), .in18(1'b1), .in19(1'b1), .in20(1'b0), .in21(1'b0), .in22(1'b1), .in23(1'b1),
    .in24(1'b1), .in25(1'b1), .in26(1'b1), .in27(1'b0), .in28(1'b1), .in29(1'b1), .in30(1'b0), .in31(1'b0),
    .out(multiplexer_7_out), .sel({V, W, X, Y, Z}), .en(1'b1));
  or or_1 (A1, and_1_out, and_2_out, and_3_out, and_4_out, and_5_out, T);
  or or_2 (B1, and_6_out, and_7_out, and_8_out, and_9_out, and_10_out, and_11_out);
  or or_3 (C1, and_12_out, and_13_out, T, U, ~V);  // OR_Gate
  or or_4 (D1, and_14_out, and_15_out, and_16_out, and_17_out, and_18_out, and_19_out, and_20_out);
  or or_5 (E1, and_21_out, and_22_out, and_23_out, and_24_out, and_25_out, and_26_out, and_27_out, and_28_out, and_29_out);
  or or_6 (F1, and_30_out, and_31_out, and_32_out, and_33_out, and_34_out, and_35_out, and_36_out);
  or or_7 (G1, and_37_out, and_38_out, and_39_out, and_40_out, U);
  Multiplexer #(.select(5)) multiplexer_8 (
    .in0(1'b1), .in1(1'b1), .in2(1'b0), .in3(1'b1), .in4(1'b1), .in5(1'b1), .in6(1'b1), .in7(1'b1),
    .in8(1'b1), .in9(1'b0), .in10(1'b1), .in11(1'b1), .in12(1'b0), .in13(1'b1), .in14(1'b1), .in15(1'b1),
    .in16(1'b1), .in17(1'b1), .in18(1'b1), .in19(1'b0), .in20(1'b1), .in21(1'b1), .in22(1'b0), .in23(1'b1),
    .in24(1'b1), .in25(1'b1), .in26(1'b1), .in27(1'b1), .in28(1'b1), .in29(1'b0), .in30(1'b1), .in31(1'b1),
    .out(multiplexer_8_out), .sel({V, W, X, Y, Z}), .en(1'b1));
  Multiplexer #(.select(5)) multiplexer_9 (
    .in0(1'b1), .in1(1'b1), .in2(1'b1), .in3(1'b0), .in4(1'b0), .in5(1'b1), .in6(1'b1), .in7(1'b1),
    .in8(1'b1), .in9(1'b1), .in10(1'b1), .in11(1'b1), .in12(1'b1), .in13(1'b0), .in14(1'b0), .in15(1'b1),
    .in16(1'b1), .in17(1'b1), .in18(1'b1), .in19(1'b1), .in20(1'b1), .in21(1'b1), .in22(1'b1), .in23(1'b0),
    .in24(1'b0), .in25(1'b1), .in26(1'b1), .in27(1'b1), .in28(1'b1), .in29(1'b1), .in30(1'b1), .in31(1'b1),
    .out(multiplexer_9_out), .sel({V, W, X, Y, Z}), .en(1'b1));
  Multiplexer #(.select(5)) multiplexer_10 (
    .in0(1'b0), .in1(1'b1), .in2(1'b1), .in3(1'b1), .in4(1'b1), .in5(1'b1), .in6(1'b1), .in7(1'b1),
    .in8(1'b1), .in9(1'b1), .in10(1'b0), .in11(1'b1), .in12(1'b1), .in13(1'b1), .in14(1'b1), .in15(1'b1),
    .in16(1'b1), .in17(1'b1), .in18(1'b1), .in19(1'b1), .in20(1'b0), .in21(1'b1), .in22(1'b1), .in23(1'b1),
    .in24(1'b1), .in25(1'b1), .in26(1'b1), .in27(1'b1), .in28(1'b1), .in29(1'b1), .in30(1'b0), .in31(1'b1),
    .out(multiplexer_10_out), .sel({V, W, X, Y, Z}), .en(1'b1));
  Multiplexer #(.select(5)) multiplexer_11 (
    .in0(1'b1), .in1(1'b1), .in2(1'b0), .in3(1'b1), .in4(1'b1), .in5(1'b0), .in6(1'b1), .in7(1'b1),
    .in8(1'b1), .in9(1'b0), .in10(1'b1), .in11(1'b1), .in12(1'b0), .in13(1'b1), .in14(1'b1), .in15(1'b0),
    .in16(1'b1), .in17(1'b1), .in18(1'b1), .in19(1'b0), .in20(1'b1), .in21(1'b1), .in22(1'b0), .in23(1'b1),
    .in24(1'b1), .in25(1'b0), .in26(1'b1), .in27(1'b1), .in28(1'b1), .in29(1'b0), .in30(1'b1), .in31(1'b1),
    .out(multiplexer_11_out), .sel({V, W, X, Y, Z}), .en(1'b1));
  Multiplexer #(.select(5)) multiplexer_12 (
    .in0(1'b1), .in1(1'b0), .in2(1'b0), .in3(1'b0), .in4(1'b1), .in5(1'b0), .in6(1'b1), .in7(1'b0),
    .in8(1'b1), .in9(1'b0), .in10(1'b1), .in11(1'b0), .in12(1'b0), .in13(1'b0), .in14(1'b1), .in15(1'b0),
    .in16(1'b1), .in17(1'b0), .in18(1'b1), .in19(1'b0), .in20(1'b1), .in21(1'b0), .in22(1'b0), .in23(1'b0),
    .in24(1'b1), .in25(1'b0), .in26(1'b1), .in27(1'b0), .in28(1'b1), .in29(1'b0), .in30(1'b1), .in31(1'b0),
    .out(multiplexer_12_out), .sel({V, W, X, Y, Z}), .en(1'b1));
  Multiplexer #(.select(5)) multiplexer_13 (
    .in0(1'b0), .in1(1'b0), .in2(1'b1), .in3(1'b1), .in4(1'b1), .in5(1'b0), .in6(1'b1), .in7(1'b1),
    .in8(1'b1), .in9(1'b0), .in10(1'b0), .in11(1'b0), .in12(1'b1), .in13(1'b1), .in14(1'b1), .in15(1'b0),
    .in16(1'b1), .in17(1'b1), .in18(1'b1), .in19(1'b0), .in20(1'b0), .in21(1'b0), .in22(1'b1), .in23(1'b1),
    .in24(1'b1), .in25(1'b0), .in26(1'b1), .in27(1'b1), .in28(1'b1), .in29(1'b0), .in30(1'b0), .in31(1'b0),
    .out(multiplexer_13_out), .sel({V, W, X, Y, Z}), .en(1'b1));
  Multiplexer #(.select(5)) multiplexer_14 (
    .in0(1'b1), .in1(1'b1), .in2(1'b1), .in3(1'b1), .in4(1'b1), .in5(1'b0), .in6(1'b1), .in7(1'b1),
    .in8(1'b0), .in9(1'b0), .in10(1'b1), .in11(1'b1), .in12(1'b1), .in13(1'b1), .in14(1'b1), .in15(1'b0),
    .in16(1'b1), .in17(1'b1), .in18(1'b0), .in19(1'b0), .in20(1'b1), .in21(1'b1), .in22(1'b1), .in23(1'b1),
    .in24(1'b1), .in25(1'b0), .in26(1'b1), .in27(1'b1), .in28(1'b0), .in29(1'b0), .in30(1'b1), .in31(1'b1),
    .out(multiplexer_14_out), .sel({V, W, X, Y, Z}), .en(1'b1));
  Multiplexer #(.select(5)) multiplexer_15 (
    .in0(1'b0), .in1(1'b1), .in2(1'b1), .in3(1'b1), .in4(1'b1), .in5(1'b1), .in6(1'b1), .in7(1'b0),
    .in8(1'b1), .in9(1'b1), .in10(1'b0), .in11(1'b1), .in12(1'b1), .in13(1'b1), .in14(1'b1), .in15(1'b1),
    .in16(1'b1), .in17(1'b0), .in18(1'b1), .in19(1'b1), .in20(1'b0), .in21(1'b1), .in22(1'b1), .in23(1'b1),
    .in24(1'b1), .in25(1'b1), .in26(1'b1), .in27(1'b0), .in28(1'b1), .in29(1'b1), .in30(1'b0), .in31(1'b1),
    .out(multiplexer_15_out), .sel({V, W, X, Y, Z}), .en(1'b1));
  Multiplexer #(.select(5)) multiplexer_16 (
    .in0(1'b1), .in1(1'b1), .in2(1'b1), .in3(1'b1), .out(multiplexer_16_out), .sel({V, W, X, Y, Z}), .en(1'b1));  // open: in4, in5, in6, in7, in8, in9, in10, in11, in12, in13, in14, in15, in16, in17, in18, in19, in20, in21, in22, in23, in24, in25, in26, in27, in28, in29, in30, in31
  Multiplexer #(.select(5)) multiplexer_17 (
    .in0(1'b0), .in1(1'b1), .in2(1'b1), .in3(1'b1), .out(multiplexer_17_out), .sel({V, W, X, Y, Z}), .en(1'b1));  // open: in4, in5, in6, in7, in8, in9, in10, in11, in12, in13, in14, in15, in16, in17, in18, in19, in20, in21, in22, in23, in24, in25, in26, in27, in28, in29, in30, in31
  Multiplexer #(.select(5)) multiplexer_18 (
    .in0(1'b1), .in1(1'b0), .in2(1'b0), .in3(1'b1), .in4(1'b1), .in5(1'b1), .in6(1'b1), .in7(1'b1),
    .in8(1'b1), .in9(1'b1), .in10(1'b1), .in11(1'b0), .in12(1'b0), .in13(1'b1), .in14(1'b1), .in15(1'b1),
    .in16(1'b1), .in17(1'b1), .in18(1'b1), .in19(1'b1), .in20(1'b1), .in21(1'b0), .in22(1'b0), .in23(1'b1),
    .in24(1'b1), .in25(1'b1), .in26(1'b1), .in27(1'b1), .in28(1'b1), .in29(1'b1), .in30(1'b1), .in31(1'b0),
    .out(multiplexer_18_out), .sel({V, W, X, Y, Z}), .en(1'b1));
  Multiplexer #(.select(5)) multiplexer_19 (
    .in0(1'b1), .in1(1'b1), .in2(1'b1), .in3(1'b1), .in4(1'b1), .in5(1'b1), .in6(1'b1), .in7(1'b1),
    .in8(1'b0), .in9(1'b1), .in10(1'b1), .in11(1'b1), .in12(1'b1), .in13(1'b1), .in14(1'b1), .in15(1'b1),
    .in16(1'b1), .in17(1'b1), .in18(1'b0), .in19(1'b1), .in20(1'b1), .in21(1'b1), .in22(1'b1), .in23(1'b1),
    .in24(1'b1), .in25(1'b1), .in26(1'b1), .in27(1'b1), .in28(1'b0), .in29(1'b1), .in30(1'b1), .in31(1'b1),
    .out(multiplexer_19_out), .sel({V, W, X, Y, Z}), .en(1'b1));
  Multiplexer #(.select(5)) multiplexer_20 (
    .in0(1'b1), .in1(1'b1), .in2(1'b1), .in3(1'b1), .out(multiplexer_20_out), .sel({V, W, X, Y, Z}), .en(1'b1));  // open: in4, in5, in6, in7, in8, in9, in10, in11, in12, in13, in14, in15, in16, in17, in18, in19, in20, in21, in22, in23, in24, in25, in26, in27, in28, in29, in30, in31
  Multiplexer #(.select(5)) multiplexer_21 (
    .in0(1'b0), .in1(1'b1), .in2(1'b1), .in3(1'b0), .in4(1'b1), .in5(1'b1), .in6(1'b1), .in7(1'b0),
    .in8(1'b1), .in9(1'b1), .in10(1'b0), .in11(1'b1), .in12(1'b1), .in13(1'b0), .in14(1'b1), .in15(1'b1),
    .in16(1'b1), .in17(1'b0), .in18(1'b1), .in19(1'b1), .in20(1'b0), .in21(1'b1), .in22(1'b1), .in23(1'b0),
    .in24(1'b1), .in25(1'b1), .in26(1'b1), .in27(1'b0), .in28(1'b1), .in29(1'b1), .in30(1'b0), .in31(1'b1),
    .out(multiplexer_21_out), .sel({V, W, X, Y, Z}), .en(1'b1));
  Multiplexer #(.select(5)) multiplexer_22 (
    .in0(1'b1), .in1(1'b0), .in2(1'b1), .in3(1'b1), .out(multiplexer_22_out), .sel({V, W, X, Y, Z}), .en(1'b1));  // open: in4, in5, in6, in7, in8, in9, in10, in11, in12, in13, in14, in15, in16, in17, in18, in19, in20, in21, in22, in23, in24, in25, in26, in27, in28, in29, in30, in31
  Multiplexer #(.select(5)) multiplexer_23 (
    .in0(1'b1), .in1(1'b0), .in2(1'b1), .in3(1'b0), .out(multiplexer_23_out), .sel({V, W, X, Y, Z}), .en(1'b1));  // open: in4, in5, in6, in7, in8, in9, in10, in11, in12, in13, in14, in15, in16, in17, in18, in19, in20, in21, in22, in23, in24, in25, in26, in27, in28, in29, in30, in31
  Multiplexer #(.select(5)) multiplexer_24 (
    .in0(1'b0), .in1(1'b0), .in2(1'b1), .in3(1'b0), .in4(1'b1), .in5(1'b0), .in6(1'b1), .in7(1'b0),
    .in8(1'b1), .in9(1'b0), .in10(1'b0), .in11(1'b0), .in12(1'b1), .in13(1'b0), .in14(1'b1), .in15(1'b0),
    .in16(1'b1), .in17(1'b0), .in18(1'b1), .in19(1'b0), .in20(1'b0), .in21(1'b0), .in22(1'b1), .in23(1'b0),
    .in24(1'b1), .in25(1'b0), .in26(1'b1), .in27(1'b0), .in28(1'b1), .in29(1'b0), .in30(1'b0), .in31(1'b0),
    .out(multiplexer_24_out), .sel({V, W, X, Y, Z}), .en(1'b1));
  Multiplexer #(.select(5)) multiplexer_25 (
    .in0(1'b1), .in1(1'b0), .in2(1'b1), .in3(1'b1), .out(multiplexer_25_out), .sel({V, W, X, Y, Z}), .en(1'b1));  // open: in4, in5, in6, in7, in8, in9, in10, in11, in12, in13, in14, in15, in16, in17, in18, in19, in20, in21, in22, in23, in24, in25, in26, in27, in28, in29, in30, in31
  Multiplexer #(.select(5)) multiplexer_26 (
    .in0(1'b1), .in1(1'b1), .in2(1'b1), .in3(1'b0), .in4(1'b1), .in5(1'b1), .in6(1'b1), .in7(1'b0),
    .in8(1'b0), .in9(1'b0), .in10(1'b1), .in11(1'b1), .in12(1'b1), .in13(1'b0), .in14(1'b1), .in15(1'b1),
    .in16(1'b1), .in17(1'b0), .in18(1'b0), .in19(1'b0), .in20(1'b1), .in21(1'b1), .in22(1'b1), .in23(1'b0),
    .in24(1'b1), .in25(1'b1), .in26(1'b1), .in27(1'b0), .in28(1'b0), .in29(1'b0), .in30(1'b1), .in31(1'b1),
    .out(multiplexer_26_out), .sel({V, W, X, Y, Z}), .en(1'b1));
  Multiplexer #(.select(5)) multiplexer_27 (
    .in0(1'b1), .in1(1'b0), .in2(1'b1), .in3(1'b1), .out(multiplexer_27_out), .sel({V, W, X, Y, Z}), .en(1'b1));  // open: in4, in5, in6, in7, in8, in9, in10, in11, in12, in13, in14, in15, in16, in17, in18, in19, in20, in21, in22, in23, in24, in25, in26, in27, in28, in29, in30, in31
  Multiplexer #(.select(5)) multiplexer_28 (
    .in0(1'b1), .in1(1'b1), .in2(1'b1), .in3(1'b0), .in4(1'b1), .in5(1'b1), .in6(1'b0), .in7(1'b0),
    .in8(1'b1), .in9(1'b1), .in10(1'b1), .in11(1'b1), .in12(1'b1), .in13(1'b0), .in14(1'b1), .in15(1'b1),
    .in16(1'b0), .in17(1'b0), .in18(1'b1), .in19(1'b1), .in20(1'b1), .in21(1'b1), .in22(1'b1), .in23(1'b0),
    .in24(1'b1), .in25(1'b1), .in26(1'b0), .in27(1'b0), .in28(1'b1), .in29(1'b1), .in30(1'b1), .in31(1'b1),
    .out(multiplexer_28_out), .sel({V, W, X, Y, Z}), .en(1'b1));
  Multiplexer #(.select(2)) multiplexer_29 (
    .in0(multiplexer_1_out), .in1(multiplexer_8_out), .in2(multiplexer_15_out), .in3(multiplexer_16_out),
    .out(A2), .sel({T, U}), .en(1'b1));
  Multiplexer #(.select(2)) multiplexer_30 (
    .in0(multiplexer_2_out), .in1(multiplexer_9_out), .in2(multiplexer_18_out), .in3(multiplexer_17_out),
    .out(B2), .sel({T, U}), .en(1'b1));
  Multiplexer #(.select(2)) multiplexer_31 (
    .in0(multiplexer_3_out), .in1(multiplexer_10_out), .in2(multiplexer_19_out), .in3(multiplexer_20_out),
    .out(C2), .sel({T, U}), .en(1'b1));
  Multiplexer #(.select(2)) multiplexer_32 (
    .in0(multiplexer_4_out), .in1(multiplexer_11_out), .in2(multiplexer_21_out), .in3(multiplexer_22_out),
    .out(D2), .sel({T, U}), .en(1'b1));
  Multiplexer #(.select(2)) multiplexer_33 (
    .in0(multiplexer_5_out), .in1(multiplexer_12_out), .in2(multiplexer_24_out), .in3(multiplexer_23_out),
    .out(E2), .sel({T, U}), .en(1'b1));
  Multiplexer #(.select(2)) multiplexer_34 (
    .in0(multiplexer_6_out), .in1(multiplexer_13_out), .in2(multiplexer_26_out), .in3(multiplexer_25_out),
    .out(F2), .sel({T, U}), .en(1'b1));
  Multiplexer #(.select(2)) multiplexer_35 (
    .in0(multiplexer_7_out), .in1(multiplexer_14_out), .in2(multiplexer_28_out), .in3(multiplexer_27_out),
    .out(G2), .sel({T, U}), .en(1'b1));
endmodule

module _99Clock (
  input  Clock_Input,
  output Reset,
  output _6,
  output _5,
  output _4,
  output _3,
  output _2,
  output _1,
  output _0
);

  Counter #(.width(7), .max('h7f)) counter_1 (
    .Q({_6, _5, _4, _3, _2, _1, _0}), .clk(Clock_Input), .clr(Reset));  // open: load, D, count, carry
  and and_1 (Reset, _6, _5, ~_4, ~_3, _2, ~_1, ~_0);  // AND_Gate
endmodule
