// Logisim project MUX_Hexadecimal_Bonus.circ as structural Verilog: 4 circuits, main circuit main
module main (
);

  wire bit_display_1_out_5, bit_display_1_out_6, bit_display_1_out_7, bit_display_1_out_8,
       bit_display_1_out_9, bit_display_1_out_10, bit_display_1_out_11, bit_display_2_out_5,
       bit_display_2_out_6, bit_display_2_out_7, bit_display_2_out_8, bit_display_2_out_9,
       bit_display_2_out_10, bit_display_2_out_11, clock_1_out, hexclock_1__0, hexclock_1__1, hexclock_1__2,
       hexclock_1__3, hexclock_1_reset, hexclock_2__0, hexclock_2__1, hexclock_2__2, hexclock_2__3;

  HexClock hexclock_1 (
    .in_1(clock_1_out), .Reset(hexclock_1_reset), ._0(hexclock_1__0), ._1(hexclock_1__1), ._2(hexclock_1__2),
    ._3(hexclock_1__3));
  Clock_part clock_1 (.out(clock_1_out));
  HexClock hexclock_2 (
    .in_1(hexclock_1_reset), ._0(hexclock_2__0), ._1(hexclock_2__1), ._2(hexclock_2__2), ._3(hexclock_2__3));  // open: Reset
  bit_display bit_display_1 (
    .out_5(bit_display_1_out_5), .out_6(bit_display_1_out_6), .out_7(bit_display_1_out_7),
    .out_8(bit_display_1_out_8), .out_9(bit_display_1_out_9), .out_10(bit_display_1_out_10),
    .out_11(bit_display_1_out_11), .W(hexclock_1__0), .X(hexclock_1__1), .Y(hexclock_1__2), .Z(hexclock_1__3));
  bit_display bit_display_2 (
    .out_5(bit_display_2_out_5), .out_6(bit_display_2_out_6), .out_7(bit_display_2_out_7),
    .out_8(bit_display_2_out_8), .out_9(bit_display_2_out_9), .out_10(bit_display_2_out_10),
    .out_11(bit_display_2_out_11), .W(hexclock_2__0), .X(hexclock_2__1), .Y(hexclock_2__2), .Z(hexclock_2__3));
  _7_Segment_Display u_7_segment_display_1 (
    .g(bit_display_1_out_11), .f(bit_display_1_out_10), .a(bit_display_1_out_5), .b(bit_display_1_out_6),
    .e(bit_display_1_out_9), .d(bit_display_1_out_8), .c(bit_display_1_out_7));  // open: dp
  _7_Segment_Display u_7_segment_display_2 (
    .g(bit_display_2_out_11), .f(bit_display_2_out_10), .a(bit_display_2_out_5), .b(bit_display_2_out_6),
    .e(bit_display_2_out_9), .d(bit_display_2_out_8), .c(bit_display_2_out_7));  // open: dp
endmodule

module bit_display (
  input  W,
  input  X,
  input  Y,
  input  Z,
  output out_5,
  output out_6,
  output out_7,
  output out_8,
  output out_9,
  output out_10,
  output out_11
);

  Multiplexer #(.select(4)) multiplexer_1 (
    .in0(1'b1), .in1(1'b0), .in2(1'b1), .in3(1'b1), .in4(1'b0), .in5(1'b1), .in6(1'b1), .in7(1'b1),
    .in8(1'b1), .in9(1'b1), .in10(1'b1), .in11(1'b0), .in12(1'b1), .in13(1'b0), .in14(1'b1), .in15(1'b1),
    .out(out_5), .sel({Z, Y, X, W}), .en(1'b1));
  Multiplexer #(.select(4)) multiplexer_2 (
    .in0(1'b1), .in1(1'b1), .in2(1'b1), .in3(1'b1), .in4(1'b1), .in5(1'b0), .in6(1'b0), .in7(1'b1),
    .in8(1'b1), .in9(1'b1), .in10(1'b1), .in11(1'b0), .in12(1'b0), .in13(1'b1), .in14(1'b0), .in15(1'b0),
    .out(out_6), .sel({Z, Y, X, W}), .en(1'b1));
  Multiplexer #(.select(4)) multiplexer_3 (
    .in0(1'b1), .in1(1'b1), .in2(1'b0), .in3(1'b1), .in4(1'b1), .in5(1'b1), .in6(1'b1), .in7(1'b1),
    .in8(1'b1), .in9(1'b1), .in10(1'b1), .in11(1'b1), .in12(1'b0), .in13(1'b1), .in14(1'b0), .in15(1'b0),
    .out(out_7), .sel({Z, Y, X, W}), .en(1'b1));
  Multiplexer #(.select(4)) multiplexer_4 (
    .in0(1'b1), .in1(1'b0), .in2(1'b1), .in3(1'b1), .in4(1'b0), .in5(1'b1), .in6(1'b1), .in7(1'b0),
    .in8(1'b1), .in9(1'b1), .in10(1'b0), .in11(1'b1), .in12(1'b1), .in13(1'b1), .in14(1'b1), .in15(1'b0),
    .out(out_8), .sel({Z, Y, X, W}), .en(1'b1));
  Multiplexer #(.select(4)) multiplexer_5 (
    .in0(1'b1), .in1(1'b0), .in2(1'b1), .in3(1'b0), .in4(1'b0), .in5(1'b0), .in6(1'b1), .in7(1'b0),
    .in8(1'b1), .in9(1'b0), .in10(1'b1), .in11(1'b1), .in12(1'b1), .in13(1'b1), .in14(1'b1), .in15(1'b1),
    .out(out_9), .sel({Z, Y, X, W}), .en(1'b1));
  Multiplexer #(.select(4)) multiplexer_6 (
    .in0(1'b1), .in1(1'b0), .in2(1'b0), .in3(1'b0), .in4(1'b1), .in5(1'b1), .in6(1'b1), .in7(1'b0),
    .in8(1'b1), .in9(1'b1), .in10(1'b1), .in11(1'b1), .in12(1'b1), .in13(1'b0), .in14(1'b1), .in15(1'b1),
    .out(out_10), .sel({Z, Y, X, W}), .en(1'b1));
  Multiplexer #(.select(4)) multiplexer_7 (
    .in0(1'b0), .in1(1'b0), .in2(1'b1), .in3(1'b1), .in4(1'b1), .in5(1'b1), .in6(1'b1), .in7(1'b0),
    .in8(1'b1), .in9(1'b1), .in10(1'b1), .in11(1'b1), .in12(1'b0), .in13(1'b1), .in14(1'b1), .in15(1'b1),
    .out(out_11), .sel({Z, Y, X, W}), .en(1'b1));
endmodule

module Clock (
  output _0,
  output _1,
  output _2,
  output _3,
  output Reset
);

  wire clock_1_out;

  Counter #(.width(4), .max('hf)) counter_1 (
    .Q({_3, _2, _1, _0}), .clk(clock_1_out), .clr(Reset));  // open: load, D, count, carry
  Clock_part clock_1 (.out(clock_1_out));
  and and_1 (Reset, ~_0, _1, ~_2, _3);  // AND_Gate
endmodule

module HexClock (
  input  in_1,
  output _0,
  output _1,
  output _2,
  output _3,
  output Reset
);

  Counter #(.width(4), .max('hf)) counter_1 (.Q({_3, _2, _1, _0}), .clk(in_1));  // open: load, D, count, carry, clr
  and and_1 (Reset, _0, _1, _2, _3);
endmodule
